# Fritzing sketch servo-externalpwr (saved by Fritzing 0.9.4)
breadboards: 1

parts:
  Part1 = Adafruit HUZZAH32 ESP32 Feather [part_number="Adafruit #3405"]
  M1 = Dagu DGServo 9g (Top view) [part_number=RS001B]

nets:
  GND: Part1.GND, M1.gnd
  3.3V: Part1.3.3V, M1.vcc
  N1: Part1.IO15_A8, M1.pulse

notes:
  servo_move.py wiring
